// Logisim project 8051.circ as structural Verilog
module ALU (
  input  CarryIn,
  input  [7:0] Accumulator,
  input  [2:0] in_3,
  input  [7:0] RegisterB,
  output CarryFlag,
  output [7:0] out_6
);

  wire [7:0] adder_1_out, adder_2_out;

  Adder adder_1 (.a(8'h1), .b(Accumulator), .out(adder_1_out), .cin(1'b0));  // open: cout
  Adder adder_2 (.a(Accumulator), .b({8{1'b1}}), .out(adder_2_out));  // open: cin, cout
  Multiplexer #(.select(3), .width(8)) multiplexer_1 (
    .in0(adder_1_out), .in1(adder_2_out), .out(out_6), .sel(in_3));  // open: in2, in3, in4, in5, in6, in7
endmodule
